# Fritzing sketch Arduino digital analog input output (saved by Fritzing 0.9.10b)
breadboards: 1

parts:
  Part1 = Arduino Uno (Rev3)
  R1 = Resistor [tolerance=±5% power=0.25 resistance=220 package=THT]
  R2 = Resistor [tolerance=±10% power=0.25 resistance=2.2k package=THT]
  U1 = POT [knob_status=50% power=0.5W package=pot_alpha_rv16af-20]
  S1 = Square Pushbutton
  R3 = Resistor [tolerance=±5% power=0.25 resistance=220 package=THT]
  LED1 = LED - 5mm [color="Red (633nm)" current=0.030 package="5 mm [THT]"]
  LED2 = LED - 5mm [color="Red (633nm)" current=0.030 package="5 mm [THT]"]

nets:
  N1: Part1.A0, U1.S
  N2: Part1.D11_PWM/MOSI, R1.Pin_1
  N3: Part1.D2, R2.Pin_0, S1.leg0
  N4: Part1.D3_PWM, R3.Pin_1
  N5: Part1.5V, R2.Pin_1, U1.E, LED2.cathode
  N6: Part1.GND, U1.A, S1.leg1, LED1.cathode
  N7: R1.Pin_0, LED1.anode
  N8: R3.Pin_0, LED2.anode

notes:
  push button
