# Fritzing sketch arduino dht11 servo buzzer (saved by Fritzing 0.9.10b)
breadboards: 1

parts:
  Part1 = Arduino Uno (Rev3)
  SERVO1 = Tower Pro SG90 servo [part_number=101246]
  DHT1 = DHT11 Humitidy and Temperature Sensor
  J1 = Piezo Speaker
  R1 = Resistor [tolerance=±5% power=0.25 resistance=220 package=THT]

nets:
  N1: Part1.D9_PWM, SERVO1.Signal
  N2: Part1.D12/MISO, DHT1.DATA
  N3: Part1.D13/SCK, R1.Pin_1
  5V: Part1.5V, SERVO1.+5V, DHT1.VDD
  GND: Part1.VIN, SERVO1.GND, DHT1.GND, J1.pin1
  N4: J1.pin2, R1.Pin_0

custom parts:
  Tower Pro SG90 servo: Original file by John De Cristofaro http://www.adafruit.com/products/1449 Adafruit Feedback Servo (Small) Edited by: e-radionica.com 28/9/2015
  DHT11 Humitidy and Temperature Sensor: DHT11 Humidity and Temperature Sensor
