# Fritzing sketch arduino_ultrasonic_buzzer (saved by Fritzing 0.9.10b)
breadboards: 1

parts:
  Part1 = Arduino Uno (Rev3)
  J1 = Piezo Speaker
  R1 = Resistor [tolerance=±5% power=0.25 resistance=220 package=THT]
  HC-SR04_Sensor_1 = HC-SR04 Ultrasonic Distance Sensor

nets:
  N1: Part1.D13/SCK, R1.Pin_1
  N2: Part1.D6_PWM, HC-SR04_Sensor_1.ECHO
  N3: Part1.D7, HC-SR04_Sensor_1.TRIG
  5V: Part1.5V, HC-SR04_Sensor_1.VCC
  VIN: Part1.VIN, J1.pin1, HC-SR04_Sensor_1.GND
  N4: J1.pin2, R1.Pin_0
