# Fritzing sketch nodemcu display sensor value control dio (saved by Fritzing 0.9.10b)
breadboards: 1

parts:
  U1 = NodeMCU V3.0
  U2 = POT [knob_status=50% power=0.5W package=pot_alpha_rv16af-20]
  LED1 = LED - 3mm [color="Red (633nm)" current=0.030 package="3 mm [THT]"]
  R1 = Resistor [tolerance=±5% power=0.25 resistance=220 package=THT]

nets:
  N1: U1.D8, R1.Pin_1
  N2: U1.3V3, U2.A
  N3: U1.GND, U2.E, LED1.cathode
  N4: U1.A0, U2.S
  N5: LED1.anode, R1.Pin_0

custom parts:
  NodeMCU V3.0: ESP8266 based NodeMCU
