# Fritzing sketch arduino_nodemcu_serial_communication_wiring (saved by Fritzing 0.9.10b)
breadboards: 1

parts:
  U1 = NodeMCU V3.0
  Part1 = Arduino Uno (Rev3)

nets:
  N1: U1.D1, Part1.D2
  N2: U1.D2, Part1.D3_PWM
  GND: U1.GND, Part1.GND

custom parts:
  NodeMCU V3.0: ESP8266 based NodeMCU
