# Fritzing sketch arduino_nodemcu_serial_communication_blynk_wiring (saved by Fritzing 0.9.10b)
breadboards: 1

parts:
  U1 = NodeMCU V3.0
  Part1 = Arduino Uno (Rev3)
  DHT1 = DHT11 Humitidy and Temperature Sensor
  SERVO1 = Tower Pro SG90 servo [part_number=101246]

nets:
  N1: U1.D1, Part1.D2
  N2: U1.D2, Part1.D3_PWM
  GND: U1.GND, Part1.GND, DHT1.GND, SERVO1.GND
  N3: Part1.D9_PWM, SERVO1.Signal
  N4: Part1.D12/MISO, DHT1.DATA
  VDD: DHT1.VDD, SERVO1.+5V

custom parts:
  NodeMCU V3.0: ESP8266 based NodeMCU
  DHT11 Humitidy and Temperature Sensor: DHT11 Humidity and Temperature Sensor
  Tower Pro SG90 servo: Original file by John De Cristofaro http://www.adafruit.com/products/1449 Adafruit Feedback Servo (Small) Edited by: e-radionica.com 28/9/2015
