# Fritzing sketch sensor actuator library (saved by Fritzing 0.9.10b)
breadboards: 1

parts:
  U2 = NodeMCU V3.0
  HC-SR04_Sensor_1 = HC-SR04 Ultrasonic Distance Sensor
  SERVO1 = Tower Pro SG90 servo [part_number=101246]

nets:
  N1: U2.D1, HC-SR04_Sensor_1.ECHO
  N2: U2.D2, HC-SR04_Sensor_1.TRIG
  N3: U2.D3, SERVO1.Signal
  GND: U2.GND, U2.VU, HC-SR04_Sensor_1.GND, SERVO1.GND
  VCC: HC-SR04_Sensor_1.VCC, SERVO1.+5V

custom parts:
  NodeMCU V3.0: ESP8266 based NodeMCU
  Tower Pro SG90 servo: Original file by John De Cristofaro http://www.adafruit.com/products/1449 Adafruit Feedback Servo (Small) Edited by: e-radionica.com 28/9/2015
